// Logisim project ex1.circ as structural Verilog: 1 circuit, main circuit generate_immediate
module generate_immediate (
  input  [31:0] INSTRUCTION,
  output [31:0] IMMEDIATE
);

  Multiplexer #(.enable("false"), .width(32)) multiplexer_1 (
    .in0({{20{1'b0}}, INSTRUCTION[31:25], INSTRUCTION[11:7]}),
    .in1({{20{1'b1}}, INSTRUCTION[31:25], INSTRUCTION[11:7]}), .out(IMMEDIATE), .sel(INSTRUCTION[31]));
endmodule
